# Fritzing sketch Boton Luz (saved by Fritzing 0.9.3b)
breadboards: 1

parts:
  Componente1 = Arduino Uno (Rev3)
  LED1 = LED - 5mm [color="Red (633nm)" package="5 mm [THT]"]  # not connected
  S1 = Pushbutton [package=THT]
  R1 = Resistor [tolerance=±5% resistance=220 package=THT]
  R2 = Resistor [tolerance=±5% resistance=220 package=THT]

nets:
  N1: Componente1.D8, S1.leg1, R1.Pin_1
  N2: Componente1.5V, S1.leg0
  N3: Componente1.GND, R1.Pin_0, R2.Pin_0
